// Logisim project ISA.circ as structural Verilog: 1 circuit, main circuit my circuit
module my_circuit (
  input  in_1,
  input  [31:0] in_2,
  input  LD_PC,
  input  LD_MAR,
  output out_5,
  output [31:0] out_6
);

  wire [31:0] PC_q;

  Register #(.width(32)) PC (.D(in_2), .Q(PC_q), .clk(LD_PC));  // open: en, clr
  Register #(.width(32)) MAR (.D(PC_q), .Q(out_6), .clk(LD_MAR));  // open: en, clr

  assign out_5 = in_1;
endmodule
